# Fritzing sketch UKWSender (saved by Fritzing 0.9.3b)
breadboards: 1

parts:
  C1 = Electrolytic Capacitor [capacitance=33µF package="0605 [SMD, electrolytic]"]
  R1 = Rotary Potentiometer (Small) [maximum_resistance=22kΩ package=THT]
  C2 = Ceramic Capacitor [capacitance=330pF package="100 mil [THT, multilayer]"]
  U1 = TRANSISTOR_NPN_2 [part_number=BC547 package=to-92]  # not connected
  R2 = Resistor [tolerance=±5% resistance=330k package="1206 [SMD]"]
  R3 = Resistor [tolerance=±5% resistance=5.6k package="1206 [SMD]"]
  C3 = Electrolytic Capacitor [capacitance=33µF package="0605 [SMD, electrolytic]"]
  C4 = Ceramic Capacitor [capacitance=330pF package="100 mil [THT, multilayer]"]
  R4 = Resistor [tolerance=±5% resistance=10k package="1206 [SMD]"]
  VCC1 = Battery block 9V
  R5 = Resistor [tolerance=±5% resistance=10k package="1206 [SMD]"]
  C5 = Ceramic Capacitor [capacitance=330pF package="100 mil [THT, multilayer]"]
  U2 = TRANSISTOR_NPN_2 [part_number=zn2219 package=to-92]
  R6 = Resistor [tolerance=±5% resistance=100 package="1206 [SMD]"]
  C6 = Ceramic Capacitor [capacitance=10pF package="100 mil [THT, multilayer]"]
  L1 = Inductor [package="1206 [SMD]"]
  Cap_Var = Variable Capacitor [capacitance=100nF max_capacitance=22pF min_capacitance=2pF voltage=35V part_number=2-22pF]
  C7 = Ceramic Capacitor [capacitance=1nF package="100 mil [THT, multilayer]"]
  C8 = Ceramic Capacitor [capacitance=10pF package="100 mil [THT, multilayer]"]
  R7 = Resistor [tolerance=±5% resistance=180 package="1206 [SMD]"]
  R8 = Resistor [tolerance=±5% resistance=150 package="1206 [SMD]"]
  C9 = Ceramic Capacitor [capacitance=10pF package="100 mil [THT, multilayer]"]
  ANT1 = Antenna
  U3 = MIC [package=mic_electret_smd]

nets:
  N1: C1.-, C2.0, R2.Pin_0
  N2: C1.+, R1.wiper
  N3: R1.leg1, U3.2
  N4: R1.leg2, C2.1, R4.Pin_1, VCC1.-, C5.1, R6.Pin_0, C7.1, R7.Pin_1, C9.1, U3.1
  N5: R2.Pin_1, R3.Pin_0, C3.+
  N6: R3.Pin_1, C4.0, VCC1.+, R5.Pin_1, L1.pin_1, Cap_Var.1, C7.0
  N7: C3.-, C4.1, R4.Pin_0, R5.Pin_0, C5.0, U2.B
  N8: U2.C, C6.0
  N9: U2.E, R6.Pin_1, C6.1, L1.pin_0, Cap_Var.0, C8.0
  N10: C8.1, R7.Pin_0, R8.Pin_0
  N11: R8.Pin_1, C9.0, ANT1.antenna_lead

notes:
  NF IN
  Coil:
  Draht: d=1,5mm^2 (230V Draht)
  Wicklung: 4
  Länge: 1,2cm
  SpuleD = M6 Schraube
